# Fritzing sketch avisa-te (saved by Fritzing 0.9.3b)
circuit board: 6.21659cm x 4.61991cm
breadboards: 1

parts:
  Wemos_d1_mini = WeMos D1 Mini
  zumbador = KY-012 Active Buzzer Module [package="Breakout board"]
  mlx90614 = BME280
  R = Resistor [tolerance=±5% resistance=220 package=THT]
  R_2 = Resistor [tolerance=±5% resistance=220 package=THT]
  vl6180x = Adafruit VL6180X Time of Flight Distance Sensor [part_number="Adafruit #3316"]
  R_3 = Resistor [tolerance=±5% resistance=220 package=THT]
  LED = RGB LED (com. cathode, rgb) [package="5 mm [THT]"]

nets:
  VIN: Wemos_d1_mini.3V3, zumbador.S, mlx90614.VIN, vl6180x.VIN
  N1: Wemos_d1_mini.D1, mlx90614.SCL, vl6180x.SCL
  N2: Wemos_d1_mini.D2, mlx90614.SDA, vl6180x.SDA
  N3: Wemos_d1_mini.D5, R_3.Pin_1
  N4: Wemos_d1_mini.D6, R.Pin_0
  N5: Wemos_d1_mini.D7, zumbador.NC
  N6: Wemos_d1_mini.D8, R_2.Pin_0
  GND: Wemos_d1_mini.G, zumbador.-, mlx90614.GND, vl6180x.GND, LED.common_cathode
  N7: R.Pin_1, LED.green_anode
  N8: R_2.Pin_1, LED.blue_anode
  N9: R_3.Pin_0, LED.red_anode

custom parts:
  KY-012 Active Buzzer Module: Active Piezoelectric Buzzer Module KY-012, it produces single-tone sound when signal is high. (Special thanks to vanepp for fixing the PCB holes and other errors)
  BME280: Temperature Humidity Barometric presure Sensor
  Adafruit VL6180X Time of Flight Distance Sensor: The VL6180X is a Time of Flight distance sensor like no other you've used! The sensor contains a very tiny invisible laser source, and a matching sensor. The VL6180X can detect the "time of flight", or how long the light has taken to bounce back to the sensor. Since it uses a very narrow light source, it is good for determining distance of only the surface directly in front of it. Unlike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
